# Fritzing sketch FSR_PressureSensorTest (saved by Fritzing 1.0.1rc)
breadboards: 1

parts:
  A1 = Particle - Photon2
  U1 = WS2812 RGB LED strip
  J1 = Basic Force Sensing Resistor (FSR) [package=THT]
  R1 = Resistor [tolerance=±5% power=0.25W resistance=220 package=THT]
  J2 = Basic Force Sensing Resistor (FSR) [package=THT]
  J3 = Basic Force Sensing Resistor (FSR) [package=THT]
  J4 = Basic Force Sensing Resistor (FSR) [package=THT]
  R2 = Resistor [tolerance=±5% power=0.25W resistance=220 package=THT]
  R3 = Resistor [tolerance=±5% power=0.25W resistance=220 package=THT]
  R4 = Resistor [tolerance=±5% power=0.25W resistance=220 package=THT]
  U2 = WS2812 RGB LED strip
  U3 = LIPO-1000mAh [package=lipo-1000]
  J5 = Camdenboss CTB0158-2 [part_number=CTB0158-2 package=THT]

nets:
  3.3V: A1.Pin_2, J1.pin_1, J2.pin_1, J3.pin_1, J4.pin_1
  GND: A1.Pin_4, U1.GND, R1.Pin_1, R2.Pin_1, R3.Pin_1, R4.Pin_1, U2.GND, U3.-, J5.pin2
  N1: A1.Pin_5, J1.pin_0, R1.Pin_0
  N2: A1.Pin_6, J2.pin_0, R2.Pin_0
  N3: A1.Pin_7, J3.pin_0, R3.Pin_0
  N4: A1.Pin_8, J4.pin_0, R4.Pin_0
  N5: A1.Pin_19, U1.DIN, U2.DIN
  N6: A1.Pin_26, J5.pin1
  5V: A1.Pin_28, A1.Pin_29, U1.VCC, U2.VCC, U3.+

notes:
  Normally Neopixels would get 5V from VUSB. In our case, we will wire them to Li+.
  LED strips can be connected to the same pin since they will do the same thing.
  +5V in from wireless charger

custom parts:
  Particle - Photon2: The Photon 2 is a microcontroller and Wi-Fi networking developed by particle. Features: 802.11a/b/g/n Wi-Fi, 2.4 GHz and 5 GHz Integrated PCB antenna Integrated U.FL connector for external antenna Integrated RF switch BLE 5 using same antenna as Wi-Fi Realtek RTL8721DM MCU ARM Cortex M33 CPU, 200 MHz 2048 KB (2 MB) user application maximum size 3072 KB (3 MB) of RAM available to user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
  WS2812 RGB LED strip: WS2812 strip
